# Fritzing sketch meterreader (saved by Fritzing 0.9.4)
circuit board: 10cm x 6cm
stripboards: 1

parts:
  part = Dual Op-Amp [part_number=LM358P package=dip08]
  R5 = Photocell (LDR) [package=THT]
  R6 = Resistor [tolerance=±5% resistance=10k package=THT]
  R7 = Resistor [tolerance=±5% resistance=30k package=THT]
  R8 = Resistor [tolerance=±5% resistance=3.9k package=THT]
  R9 = Resistor [tolerance=±5% resistance=150 package=THT]
  RaspiZero_W = Raspberry Pi Zero

nets:
  N1: part.A_OUT, R9.Pin_1, RaspiZero_W.pin_11
  N2: part.A_-IN, R7.Pin_1, R8.Pin_1
  N3: part.A_+IN, R5.pin_1, R6.Pin_0
  N4: part.A_V-, R6.Pin_1, R8.Pin_0, R9.Pin_0, RaspiZero_W.pin_9, RaspiZero_W.pin_34
  N5: part.A_V+, R5.pin_0, R7.Pin_0, RaspiZero_W.pin_1
